// Logisim project 实验07.circ as structural Verilog: 4 circuits, main circuit main
module main (
  input  in_1,
  input  in_2,
  input  in_3,
  input  in_4,
  input  in_5,
  input  in_6,
  input  in_7,
  input  in_8
);

  wire button_1_out, clock_1_out, fpga_1_out_18, fpga_1_out_19, fpga_1_out_20, fpga_1_out_21, fpga_1_out_22,
       fpga_1_out_23, fpga_1_out_24, fpga_1_out_25;
  wire [2:0] fpga_1_out_13;
  wire [3:0] demultiplexer_1_out0, demultiplexer_1_out1, demultiplexer_1_out2, demultiplexer_1_out3,
       demultiplexer_1_out4, demultiplexer_1_out5, demultiplexer_1_out6, demultiplexer_1_out7, fpga_1_out_17;

  LED led_1 (.in(fpga_1_out_19));
  LED led_2 (.in(fpga_1_out_20));
  LED led_3 (.in(fpga_1_out_18));
  FPGA fpga_1 (
    .in_3(in_1), .in_4(in_2), .in_1(button_1_out), .in_5(in_3), .in_6(in_4), .in_7(in_5), .in_8(in_6),
    .in_9(in_7), .in_10(in_8), .out_18(fpga_1_out_18), .out_19(fpga_1_out_19), .out_20(fpga_1_out_20),
    .out_21(fpga_1_out_21), .out_22(fpga_1_out_22), .out_23(fpga_1_out_23), .out_24(fpga_1_out_24),
    .out_25(fpga_1_out_25), .out_11(fpga_1_out_13[2]), .out_12(fpga_1_out_13[1]), .out_13(fpga_1_out_13[0]),
    .out_14(fpga_1_out_17[3]), .out_15(fpga_1_out_17[2]), .out_16(fpga_1_out_17[1]),
    .out_17(fpga_1_out_17[0]), .in_2(clock_1_out));
  LED led_4 (.in(fpga_1_out_22));
  LED led_5 (.in(fpga_1_out_24));
  LED led_6 (.in(fpga_1_out_23));
  LED led_7 (.in(fpga_1_out_21));
  LED led_8 (.in(fpga_1_out_25));
  Clock clock_1 (.out(clock_1_out));
  Button button_1 (.out(button_1_out));
  Demultiplexer #(.select(3), .width(4), .tristate("true"), .enable("false")) demultiplexer_1 (
    .out0(demultiplexer_1_out0), .out1(demultiplexer_1_out1), .out2(demultiplexer_1_out2),
    .out3(demultiplexer_1_out3), .out4(demultiplexer_1_out4), .out5(demultiplexer_1_out5),
    .out6(demultiplexer_1_out6), .out7(demultiplexer_1_out7), .in(fpga_1_out_17), .sel(fpga_1_out_13));
  Hex_Digit_Display hex_digit_display_1 (.value(demultiplexer_1_out7));  // open: dp
  Hex_Digit_Display hex_digit_display_2 (.value(demultiplexer_1_out6));  // open: dp
  Hex_Digit_Display hex_digit_display_3 (.value(demultiplexer_1_out5));  // open: dp
  Hex_Digit_Display hex_digit_display_4 (.value(demultiplexer_1_out4));  // open: dp
  Hex_Digit_Display hex_digit_display_5 (.value(demultiplexer_1_out2));  // open: dp
  Hex_Digit_Display hex_digit_display_6 (.value(demultiplexer_1_out3));  // open: dp
  Hex_Digit_Display hex_digit_display_7 (.value(demultiplexer_1_out1));  // open: dp
  Hex_Digit_Display hex_digit_display_8 (.value(demultiplexer_1_out0));  // open: dp
endmodule

module FPGA (
  input  in_1,
  input  in_2,
  input  in_3,
  input  in_4,
  input  in_5,
  input  in_6,
  input  in_7,
  input  in_8,
  input  in_9,
  input  in_10,
  output out_11,
  output out_12,
  output out_13,
  output out_14,
  output out_15,
  output out_16,
  output out_17,
  output out_18,
  output out_19,
  output out_20,
  output out_21,
  output out_22,
  output out_23,
  output out_24,
  output out_25
);

  Counter #(.width(3), .max('h7)) counter_1 (
    .Q({out_11, out_12, out_13}), .clk(in_2), .clr(in_1));  // open: load, D, count, carry
  Register register_1 (
    .D({in_3, in_4, in_5, in_6, in_7, in_8, in_9, in_10}),
    .Q({out_18, out_19, out_20, out_21, out_22, out_23, out_24, out_25}), .clk(in_2), .clr(in_1));  // open: en
  ROM #(.addrWidth(3), .dataWidth(4)) rom_1 (
    .addr({out_11, out_12, out_13}), .data({out_14, out_15, out_16, out_17}));  // open: sel
  // Probe on {out_11, out_12, out_13}
  // Probe on {out_14, out_15, out_16, out_17}

  // Other names for the same wires on the sheet: _1个按键 = in_1; _1个时钟 = in_2;
  //   _8个LED[7:0] = {out_18, out_19, out_20, out_21, out_22, out_23, out_24, out_25};
  //   _8个拨动开关[7:0] = {in_3, in_4, in_5, in_6, in_7, in_8, in_9, in_10}; 数码管使能[2:0] = {out_11, out_12, out_13};
  //   数码管数据[3:0] = {out_14, out_15, out_16, out_17}

  // Notes on the sheet:
  //   输入引脚区域
  //   电路绘制区域
  //   contents of rom_1 (hex, n*v repeats v):
  //   7 1 1 1 2 2 0 2
  //   输出引脚区域
endmodule

module CLK (
  output out_1
);

  Clock clock_1 (.out(out_1));
endmodule

module \数码管  (
  input  A,
  input  B,
  input  C,
  input  D,
  input  E,
  input  F,
  input  G,
  input  DP
);

  _7_Segment_Display u_7_segment_display_1 (.g(G), .f(F), .a(A), .b(B), .e(E), .d(D), .c(C), .dp(DP));
endmodule
