// Logisim project lab8t2.circ as structural Verilog
module dlatch (
  input  CLK,
  input  D,
  input  rst,
  output Q,
  output QN
);

  wire nand_1_out, nand_2_out, nand_3_out, nand_4_out, not_1_out;

  not not_1 (not_1_out, rst);
  nand nand_1 (nand_1_out, nand_4_out, nand_2_out);
  nand nand_2 (nand_2_out, nand_1_out, CLK, not_1_out);
  nand nand_3 (nand_3_out, nand_2_out, CLK, nand_4_out);
  nand nand_4 (nand_4_out, nand_3_out, D, not_1_out);
  nand nand_5 (Q, nand_2_out, QN);
  nand nand_6 (QN, Q, nand_3_out, not_1_out);

  // Notes on the sheet:
  //   具有异步复位功能的D触发器
endmodule

module _4bitdlatch (
  input  [3:0] D_IN,
  input  CLK,
  input  rst,
  output [3:0] D_OUT
);

  dlatch dlatch_1 (.CLK(CLK), .D(D_IN[3]), .rst(rst), .Q(D_OUT[3]));  // open: QN
  dlatch dlatch_2 (.CLK(CLK), .D(D_IN[2]), .rst(rst), .Q(D_OUT[2]));  // open: QN
  dlatch dlatch_3 (.CLK(CLK), .D(D_IN[1]), .rst(rst), .Q(D_OUT[1]));  // open: QN
  dlatch dlatch_4 (.CLK(CLK), .D(D_IN[0]), .rst(rst), .Q(D_OUT[0]));  // open: QN

  // Notes on the sheet:
  //   带有异步复位功能的四位寄存器
endmodule

module jishuqi (
  input  [3:0] in_1,
  input  rst,
  input  sw,
  output [3:0] out_4
);

  wire clk_out, d_ff_1_q, xor_1_out;
  wire [3:0] adder_1_out, multiplexer_1_out;

  Adder #(.width(4)) adder_1 (.a(out_4), .b(in_1), .out(adder_1_out), .cin(1'b0));  // open: cout
  D_Flip_Flop d_ff_1 (.clk(clk_out), .D(sw), .Q(d_ff_1_q));  // open: Qn, preset, en, reset
  Multiplexer #(.width(4)) multiplexer_1 (
    .in0(out_4), .in1(adder_1_out), .out(multiplexer_1_out), .sel(xor_1_out));  // open: en
  xor xor_1 (xor_1_out, sw, d_ff_1_q);
  Clock clk (.out(clk_out));
  _4bitdlatch u_4bitdlatch_1 (.D_IN(multiplexer_1_out), .CLK(clk_out), .rst(rst), .D_OUT(out_4));

  // Notes on the sheet:
  //   计数器
endmodule
